// Logisim project Controller.circ as structural Verilog: 11 circuits, main circuit main
module main (
  input  [15:0] Inst,
  input  [3:0] Flags,
  input  Reset,
  output Carry,
  output DP_Shift,
  output Imm32_Enable,
  output [4:0] Imm5,
  output [31:0] Imm32,
  output [3:0] ALU_Opcode,
  output [2:0] Rm,
  output [2:0] Rn,
  output [2:0] Rd,
  output [31:0] RAM_Addr,
  output Load,
  output Store,
  output [7:0] PC
);

  wire BrE, CARRY1, CARRY2, clk, DPE, LSE, opcode_decoder_1_shift, PC_HOLD, SPAE, WE;
  wire [2:0] RD1, RD2, RD3, RM1, RM2, RM3, RN1, RN2;
  wire [3:0] ALU_OPCODE1, ALU_OPCODE2, flags_apsr_1_flags_out, FLAGS_UM1, FLAGS_UM2, FUME;
  wire [31:0] NSP, SP;

  Clock u_Clk (.out(clk));
  assign FUME = FLAGS_UM1 | FLAGS_UM2;  // OR_Gate or_1, 4 bits wide
  Opcode_Decoder opcode_decoder_1 (
    .SP_Address(SPAE), .Branch(BrE), .Load_Store(LSE), .Data_Processing(DPE), .Shift(opcode_decoder_1_shift));  // open: Opcode
  Data_Processing data_processing_1 (
    .Instruction(Inst), .Enable(DPE), .ALU_Opcode(ALU_OPCODE2), .Rm(RM2), .Rn(RN2), .Rd(RD3),
    .Flags_Update_Mask(FLAGS_UM2));
  SP_Address sp_address_1 (
    .Instruction(Inst), .Enable(SPAE), .Stack_Pointer(SP), .Write_Enable(WE), .New_Stack_Pointer(NSP));
  Flags_APSR flags_apsr_1 (
    .Flags_In(Flags), .Update_Mask(FUME), .Clk(clk), .Reset(Reset), .Flags_Out(flags_apsr_1_flags_out));
  Shift_Add_SUb_Mov shift_add_sub_mov_1 (
    .Instruction(Inst), .Enable(opcode_decoder_1_shift), .ALU_Opcode(ALU_OPCODE1), .Rm(RM1), .Rn(RN1),
    .Rd(RD1), .Flags_Update_Mask(FLAGS_UM1), .Carry(CARRY1), .Imm32_Enable(Imm32_Enable), .Imm5(Imm5),
    .Imm32(Imm32));
  Load_Store load_store_1 (
    .Instruction(Inst), .Enable(LSE), .Stack_Pointer(SP), .Clk(clk), .Reset(Reset), .Store(Store),
    .Load(Load), .PC_Hold(PC_HOLD), .Rm(RM3), .Rd(RD2), .RAM_Addr(RAM_Addr));
  Conditional conditional_1 (
    .Instruction(Inst), .Enable(BrE), .N(flags_apsr_1_flags_out[0]), .Z(flags_apsr_1_flags_out[1]),
    .C(flags_apsr_1_flags_out[2]), .V(flags_apsr_1_flags_out[3]));  // open: Verified, Offset
  Adder adder_1 ();  // open: a, b, out, cin, cout
  assign ALU_Opcode = ALU_OPCODE1 | ALU_OPCODE2;  // OR_Gate or_2, 4 bits wide
  Program_Counter program_counter_1 (
    .Clk(clk), .Outputt(PC), .Carry(CARRY2));  // open: Data, Count, UpDown, Load, Clear
  Stack_Pointer stack_pointer_1 (.Data(NSP), .Enable(WE), .Clk(clk), .Reset(Reset), .Outputt(SP));
  or or_3 (Carry, CARRY1, CARRY2);
  assign Rm = RM1 | RM2 | RM3;  // OR_Gate or_4, 3 bits wide
  assign Rn = RN1 | RN2;  // OR_Gate or_5, 3 bits wide
  assign Rd = RD1 | RD2 | RD3;  // OR_Gate or_6, 3 bits wide

  // Other names for the same wires on the sheet: ENABLE32 = Imm32_Enable; I[15:0] = Inst; A[5:0] = Inst[15:10]
endmodule

module Opcode_Decoder (
  input  [5:0] Opcode,
  output Shift,
  output Data_Processing,
  output Load_Store,
  output SP_Address,
  output Branch
);

  Opcode_Decoder_Sub1 opcode_decoder_sub1_1 (
    .f(Opcode[5]), .e(Opcode[4]), .d(Opcode[3]), .c(Opcode[2]), .b(Opcode[1]), .a(Opcode[0]), .shift(Shift),
    .data_processing(Data_Processing), .load_store(Load_Store), .sp_address(SP_Address), .branch(Branch));

  // Other names for the same wires on the sheet: a = Opcode[0]; b = Opcode[1]; c = Opcode[2]; d = Opcode[3];
  //   e = Opcode[4]; f = Opcode[5]
endmodule

module Shift_Add_SUb_Mov (
  input  [15:0] Instruction,
  input  Enable,
  output [3:0] ALU_Opcode,
  output [2:0] Rm,
  output [2:0] Rn,
  output [2:0] Rd,
  output [3:0] Flags_Update_Mask,
  output Carry,
  output Imm32_Enable,
  output [4:0] Imm5,
  output [31:0] Imm32
);
endmodule

module Data_Processing (
  input  [15:0] Instruction,
  input  Enable,
  output [3:0] ALU_Opcode,
  output [2:0] Rm,
  output [2:0] Rn,
  output [2:0] Rd,
  output [3:0] Flags_Update_Mask
);

  wire [2:0] undriven, undriven_2;

  assign Rm = undriven & undriven_2;  // AND_Gate and_1, 3 bits wide

  // Other names for the same wires on the sheet: Code[3:0] = Instruction[9:6]; Rdn[2:0] = Instruction[2:0];
  //   Rm_t[2:0] = Instruction[5:3]
endmodule

module Flags_APSR (
  input  [3:0] Flags_In,
  input  [3:0] Update_Mask,
  input  Clk,
  input  Reset,
  output [3:0] Flags_Out
);

  Register #(.width(1)) N (.D(Flags_In[0]), .en(Update_Mask[0]), .clk(Clk), .Q(Flags_Out[0]), .clr(Reset));
  Register #(.width(1)) Z (.D(Flags_In[1]), .en(Update_Mask[1]), .clk(Clk), .Q(Flags_Out[1]), .clr(Reset));
  Register #(.width(1)) C (.D(Flags_In[2]), .en(Update_Mask[2]), .clk(Clk), .Q(Flags_Out[2]), .clr(Reset));
  Register #(.width(1)) V (.D(Flags_In[3]), .en(Update_Mask[3]), .clk(Clk), .Q(Flags_Out[3]), .clr(Reset));

  // Other names for the same wires on the sheet: n = Flags_Out[0]; z = Flags_Out[1]; c = Flags_Out[2];
  //   v = Flags_Out[3]
endmodule

module Load_Store (
  input  [15:0] Instruction,
  input  Enable,
  input  [31:0] Stack_Pointer,
  input  Clk,
  input  Reset,
  output Store,
  output Load,
  output PC_Hold,
  output [2:0] Rm,
  output [2:0] Rd,
  output [31:0] RAM_Addr
);
endmodule

module SP_Address (
  input  [15:0] Instruction,
  input  Enable,
  input  [31:0] Stack_Pointer,
  output Write_Enable,
  output [31:0] New_Stack_Pointer
);
endmodule

module Conditional (
  input  [15:0] Instruction,
  input  Enable,
  input  N,
  input  Z,
  input  C,
  input  V,
  output Verified,
  output [7:0] Offset
);
endmodule

module Program_Counter (
  input  [7:0] Data,
  input  Count,
  input  UpDown,
  input  Load,
  input  Clk,
  input  Clear,
  output [7:0] Outputt,
  output Carry
);
endmodule

module Stack_Pointer (
  input  [31:0] Data,
  input  Enable,
  input  Clk,
  input  Reset,
  output [31:0] Outputt
);
endmodule

module Opcode_Decoder_Sub1 (
  input  f,
  input  e,
  input  d,
  input  c,
  input  b,
  input  a,
  output shift,
  output data_processing,
  output load_store,
  output sp_address,
  output branch
);

  wire not_1_out, not_2_out, not_3_out, not_4_out, not_5_out, not_6_out, not_7_out, not_8_out, not_9_out,
       not_10_out, not_11_out;

  not not_1 (not_1_out, f);
  not not_2 (not_2_out, e);
  not not_3 (not_3_out, f);
  not not_4 (not_4_out, d);
  not not_5 (not_5_out, c);
  not not_6 (not_6_out, b);
  not not_7 (not_7_out, a);
  not not_8 (not_8_out, e);
  not not_9 (not_9_out, d);
  not not_10 (not_10_out, e);
  not not_11 (not_11_out, d);
  and and_1 (shift, not_1_out, not_2_out);
  and and_2 (data_processing, not_3_out, e, not_4_out, not_5_out, not_6_out, not_7_out);
  and and_3 (load_store, f, not_8_out, not_9_out, c);
  and and_4 (sp_address, f, not_10_out, d, c);
  and and_5 (branch, f, e, not_11_out, c);
endmodule
