// Logisim project alutest.circ as structural Verilog: 2 circuits, main circuit ALU
// carry
module ALU (
  input  [31:0] A,
  input  [31:0] B,
  input  Retenue,
  input  [4:0] Shift,
  input  [3:0] codop,
  output [31:0] Resultat,
  output [3:0] Drapeau
);

  wire Retenue1, Retenue2, Retenue3, Retenue4, Retenue5, Retenue6;
  wire [31:0] eight, eleven, fifteen, five, four, fourteen, nine, not_1_out, one, seven, six, sixteen, ten,
       thirteen, three, twelve, two;

  BitSelector #(.width(32)) bitselector_1 (.in(B), .out(Retenue1), .sel({5{1'b1}}));
  BitSelector #(.width(32)) bitselector_2 (.in(B), .out(Retenue2), .sel({5{1'b1}}));
  BitSelector #(.width(32)) bitselector_3 (.in(B), .out(Retenue3), .sel({5{1'b1}}));
  Subtractor #(.width(32)) subtractor_1 (.a(A), .b(B), .out(seven), .bin(Retenue), .bout(Retenue5));
  BitSelector #(.width(32)) bitselector_4 (.in(B), .out(Retenue6), .sel({5{1'b1}}));
  Adder #(.width(32)) adder_1 (.a(A), .b(B), .out(six), .cin(Retenue), .cout(Retenue4));
  Subtractor #(.width(32)) subtractor_2 (.a({32{1'b0}}), .b(A), .out(ten));  // open: bin, bout
  assign one = A & B;  // AND_Gate and_1, 32 bits wide
  assign two = A ^ B;  // XOR_Gate xor_1, 32 bits wide
  Shifter #(.width(32)) shifter_1 (.in(B), .\dist (Shift), .out(three));
  Shifter #(.width(32), .shift("lr")) shifter_2 (.in(B), .\dist (Shift), .out(four));
  Shifter #(.width(32), .shift("ar")) shifter_3 (.in(B), .\dist (Shift), .out(five));
  Shifter #(.width(32), .shift("rr")) shifter_4 (.in(B), .\dist (Shift), .out(eight));
  assign nine = B;  // AND_Gate and_2, 32 bits wide AND_Gate
  Subtractor #(.width(32)) subtractor_3 (.a(A), .b(B), .out(eleven));  // open: bin, bout
  Adder #(.width(32)) adder_2 (.a(A), .b(B), .out(twelve));  // open: cin, cout
  assign thirteen = A | B;  // OR_Gate or_1, 32 bits wide
  assign not_1_out = ~B;  // NOT_Gate not_1, 32 bits wide
  assign sixteen = ~B;  // NOT_Gate not_2, 32 bits wide
  assign fifteen = A & not_1_out;  // AND_Gate and_3, 32 bits wide
  Multiplexer #(.select(4), .width(32), .enable("false")) multiplexer_1 (
    .in0(one), .in1(two), .in2(three), .in3(four), .in4(five), .in5(six), .in6(seven), .in7(eight),
    .in8(nine), .in9(ten), .in10(eleven), .in11(twelve), .in12(thirteen), .in13(fourteen), .in14(fifteen),
    .in15(sixteen), .out(Resultat), .sel(codop));
  Comparator #(.width(32)) comparator_1 (.a(Resultat), .b({32{1'b0}}), .eq(Drapeau[1]));  // open: gt, lt
  Multiplexer #(.select(4), .enable("false")) multiplexer_2 (
    .in2(Retenue1), .in3(Retenue2), .in4(Retenue3), .in5(Retenue4), .in6(Retenue5), .in7(Retenue6),
    .out(Drapeau[2]));  // open: in0, in1, in8, in9, in10, in11, in12, in13, in14, in15, sel
  mul32 mul32_1 (.in_1(A), .in_2(B), .out_3(fourteen));
  BitSelector #(.width(32)) bitselector_5 (.in(Resultat), .out(Drapeau[0]), .sel({5{1'b1}}));

  // Other names for the same wires on the sheet: carryin1 = Retenue

  // Notes on the sheet:
  //   N egatif
  //   Z ero
  //   C Carry
  //   V oVerflow
endmodule

module mul32 (
  input  [31:0] in_1,
  input  [31:0] in_2,
  output [31:0] out_3
);

  wire bitselector_1_out, bitselector_4_out;
  wire [30:0] adder_1_out, adder_2_out, bit_extender_1_out, bit_extender_2_out, bitselector_2_out,
       bitselector_3_out, multiplier_1_out, multiplier_2_out, multiplier_3_out, multiplier_4_out;
  wire [31:0] bit_extender_3_out, bit_extender_4_out;

  BitSelector #(.width(32)) bitselector_1 (.in(in_1), .out(bitselector_1_out), .sel({5{1'b1}}));
  BitSelector #(.width(32), .group(31)) bitselector_2 (.in(in_1), .out(bitselector_2_out), .sel(1'b0));
  BitSelector #(.width(32), .group(31)) bitselector_3 (.in(in_2), .out(bitselector_3_out), .sel(1'b0));
  // Probe on bit_extender_1_out
  BitSelector #(.width(32)) bitselector_4 (.in(in_2), .out(bitselector_4_out), .sel({5{1'b1}}));
  assign bit_extender_1_out = {{30{bitselector_1_out}}, bitselector_1_out};  // Bit_Extender bit_extender_1
  // Probe on bitselector_3_out
  // Probe on bitselector_2_out
  // Probe on bitselector_3_out
  Multiplier #(.width(31)) multiplier_1 (
    .a(bitselector_2_out), .b(bitselector_3_out), .out(multiplier_1_out));  // open: cin, cout
  // Probe on bitselector_2_out
  assign bit_extender_2_out = {{30{bitselector_4_out}}, bitselector_4_out};  // Bit_Extender bit_extender_2
  Multiplier #(.width(31)) multiplier_2 (
    .a(bit_extender_1_out), .b(bitselector_3_out), .out(multiplier_2_out), .cin({31{1'b0}}));  // open: cout
  // Probe on nothing
  Multiplier #(.width(31)) multiplier_3 (
    .a(bitselector_2_out), .b(bit_extender_2_out), .out(multiplier_3_out));  // open: cin, cout
  // Probe on bit_extender_2_out
  // Probe on multiplier_2_out
  // Probe on multiplier_3_out
  // Probe on multiplier_1_out
  Adder #(.width(31)) adder_1 (.a(multiplier_2_out), .b(multiplier_1_out), .out(adder_1_out));  // open: cin, cout
  // Probe on bit_extender_1_out
  assign bit_extender_3_out = {{1{adder_1_out[30]}}, adder_1_out};  // Bit_Extender bit_extender_3
  Multiplier #(.width(31)) multiplier_4 (
    .a(bit_extender_1_out), .b(bit_extender_2_out), .out(multiplier_4_out));  // open: cin, cout
  Adder #(.width(31)) adder_2 (.a(multiplier_4_out), .b(multiplier_3_out), .out(adder_2_out));  // open: cin, cout
  // Probe on bit_extender_2_out
  assign bit_extender_4_out = {{1{adder_2_out[30]}}, adder_2_out};  // Bit_Extender bit_extender_4
  // Probe on bit_extender_3_out
  Adder #(.width(32)) adder_3 (.a(bit_extender_3_out), .b(bit_extender_4_out), .out(out_3));  // open: cin, cout
  // Probe on bit_extender_4_out
endmodule
