// Logisim project banc.circ as structural Verilog: 1 circuit, main circuit main
module main (
  input  in_1,
  input  [2:0] RegDest,
  input  reset,
  input  [2:0] RegA,
  input  [31:0] DataIn,
  input  clk,
  input  [2:0] RegB,
  output [31:0] R_0,
  output [31:0] R_1,
  output [31:0] R_2,
  output [31:0] Aout,
  output [31:0] R_3,
  output [31:0] Bout,
  output [31:0] R_4,
  output [31:0] R_5,
  output [31:0] R_6,
  output [31:0] R_7
);

  wire demultiplexer_1_out0, demultiplexer_1_out1, demultiplexer_1_out2, demultiplexer_1_out3,
       demultiplexer_1_out4, demultiplexer_1_out5, demultiplexer_1_out6, demultiplexer_1_out7;

  Demultiplexer #(.select(3), .enable("false")) demultiplexer_1 (
    .out0(demultiplexer_1_out0), .out1(demultiplexer_1_out1), .out2(demultiplexer_1_out2),
    .out3(demultiplexer_1_out3), .out4(demultiplexer_1_out4), .out5(demultiplexer_1_out5),
    .out6(demultiplexer_1_out6), .out7(demultiplexer_1_out7), .in(in_1), .sel(RegDest));
  Register #(.width(32)) R0 (.D(DataIn), .en(demultiplexer_1_out0), .clk(clk), .Q(R_0), .clr(reset));
  Register #(.width(32)) R1 (.D(DataIn), .en(demultiplexer_1_out1), .clk(clk), .Q(R_1), .clr(reset));
  Register #(.width(32)) R2 (.D(DataIn), .en(demultiplexer_1_out2), .clk(clk), .Q(R_2), .clr(reset));
  Register #(.width(32)) R3 (.D(DataIn), .en(demultiplexer_1_out3), .clk(clk), .Q(R_3), .clr(reset));
  Register #(.width(32)) R4 (.D(DataIn), .en(demultiplexer_1_out4), .clk(clk), .Q(R_4), .clr(reset));
  Register #(.width(32)) R5 (.D(DataIn), .en(demultiplexer_1_out5), .clk(clk), .Q(R_5), .clr(reset));
  Register #(.width(32)) R6 (.D(DataIn), .en(demultiplexer_1_out6), .clk(clk), .Q(R_6), .clr(reset));
  Register #(.width(32)) R7 (.D(DataIn), .en(demultiplexer_1_out7), .clk(clk), .Q(R_7), .clr(reset));
  Multiplexer #(.select(3), .width(32), .disabled("Z"), .enable("false")) multiplexer_1 (
    .in0(R_0), .in1(R_1), .in2(R_2), .in3(R_3), .in4(R_4), .in5(R_5), .in6(R_6), .in7(R_7), .out(Aout),
    .sel(RegA));
  Multiplexer #(.select(3), .width(32), .enable("false")) multiplexer_2 (
    .in0(R_0), .in1(R_1), .in2(R_2), .in3(R_3), .in4(R_4), .in5(R_5), .in6(R_6), .in7(R_7), .out(Bout),
    .sel(RegB));

  // Other names for the same wires on the sheet: R0[31:0] = R_0; R1[31:0] = R_1; R2[31:0] = R_2; R3[31:0] = R_3;
  //   R4[31:0] = R_4; R5[31:0] = R_5; R6[31:0] = R_6; R7[31:0] = R_7
endmodule
